# Fritzing sketch hardware_simulator_for_upload (saved by Fritzing 0.9.4)
breadboards: 2

parts:
  U1 = ESP32-38PinWide [part_number=ESP32-38PinWide]
  R1 = Rotary Potentiometer (Small) [maximum_resistance=100kΩ package=THT]
  R2 = Rotary Potentiometer (Small) [maximum_resistance=100kΩ package=THT]
  R3 = Rotary Potentiometer (Small) [maximum_resistance=100kΩ package=THT]
  R4 = Rotary Potentiometer (Small) [maximum_resistance=100kΩ package=THT]
  R5 = Rotary Potentiometer (Small) [maximum_resistance=100kΩ package=THT]
  S1 = Pushbutton [package="[THT]"]
  S2 = Pushbutton [package="[THT]"]
  S3 = Pushbutton [package="[THT]"]
  S4 = Pushbutton [package="[THT]"]
  S5 = Pushbutton [package="[THT]"]
  U4 = ESP32-38PinWide [part_number=ESP32-38PinWide]
  R6 = Resistor [tolerance=±5% resistance=220 package=THT]
  D3 = Diode [package=diode-hv]
  D4 = Diode [package=diode-hv]

nets:
  N1: U1.3.3, R1.leg2, R2.leg2, R3.leg2, R4.leg2, R5.leg2, U4.3.3, U4.EN, R6.Pin_0
  N2: U1.GPIO34, R1.wiper
  N3: U1.GPIO35, R2.wiper
  N4: U1.GPIO32, R3.wiper
  N5: U1.GPIO33, R4.wiper
  N6: U1.GPIO25, R5.wiper
  N7: U1.GPIO5, S1.Pin_3, S1.Pin_4
  N8: U1.GPIO18, S3.Pin_3, S3.Pin_4
  N9: U1.GPIO19, S5.Pin_3, S5.Pin_4
  N10: U1.GPIO21, S4.Pin_3, S4.Pin_4
  N11: U1.GPIO3, U4.GPIO21, U4.GPIO3, R6.Pin_1, D3.A, D4.A
  N12: U1.GPIO22, S2.Pin_3, S2.Pin_4
  GND: U1.GND, R1.leg1, R2.leg1, R3.leg1, R4.leg1, R5.leg1, S1.Pin_1, S1.Pin_2, S2.Pin_1, S2.Pin_2, S3.Pin_1, S3.Pin_2, S4.Pin_1, S4.Pin_2, S5.Pin_1, S5.Pin_2, U4.GND

custom parts:
  ESP32-38PinWide: Generic 38-Pin ESP32 with wide format (only access to one side of pins on a breadboard) based on Stephen Lilley's HiLetgo ESP-WROOM-32 ESP32 ESP-32S Development Board.
